# Fritzing sketch schema (saved by Fritzing 0.9.5d)

parts:
  U1 = AD9833 Module
  Part1 = Arduino Yun
  FC-1 = Sound Sensor
  R1 = Resistor [tolerance=±5% resistance=220 package=THT]
  Part2 = Arduino Uno (Rev3)
  R2 = Rotary Potentiometer (Small) [maximum_resistance=100kΩ package=THT]
  U2 = AD9833 Module
  U3 = AD9833 Module
  R3 = Rotary Potentiometer (Small) [maximum_resistance=100kΩ package=THT]
  Part3 = Arduino Yun

nets:
  VCC: U1.VCC, Part1.5V
  GND: U1.DGND, Part1.GND, FC-1.GND
  N1: U1.SDATA, Part1.ICSP_MOSI
  N2: U1.SCLK, Part1.ICSP_SCK
  N3: Part1.A1, FC-1.OUT
  N4: Part1.D3_PWM, R1.Pin_0
  N5: Part1.D5_PWM, R1.Pin_1
  N6: Part1.D7, FC-1.VCC
  N7: Part2.A0, R2.wiper
  N8: Part2.D10_PWM/SS, U2.FSYNC
  N9: Part2.D11_PWM/MOSI, U2.SDATA
  N10: Part2.D13/SCK, U2.SCLK
  5V: Part2.5V, R2.leg2, U2.VCC
  N11: Part2.GND, R2.leg1, U2.DGND
  VCC_2: U3.VCC, R3.leg2, Part3.5V
  N12: U3.DGND, R3.leg1, Part3.GND
  N13: U3.SDATA, Part3.ICSP_MOSI
  N14: U3.SCLK, Part3.ICSP_SCK
  N15: R3.wiper, Part3.A0

custom parts:
  AD9833 Module: programmable waveform generator
