# Fritzing sketch schema_arduino_nuovo (saved by Fritzing 0.9.4)

parts:
  Part1 = Arduino Uno (Rev3)
  S1 = Toggle Switch [package=THT]
  R1 = Resistor [tolerance=±5% resistance=220 package=THT]
  FC-1 = Sound Sensor
  U1 = AD9833 Module

nets:
  N1: Part1.A0, FC-1.OUT
  N2: Part1.D10_PWM/SS, U1.FSYNC
  N3: Part1.D11_PWM/MOSI, U1.SDATA
  N4: Part1.D13/SCK, U1.SCLK
  N5: Part1.D3_PWM, S1.COM
  N6: Part1.D5_PWM, R1.Pin_1
  VCC: Part1.5V, FC-1.VCC, U1.VCC
  GND: Part1.GND, FC-1.GND, U1.DGND

custom parts:
  AD9833 Module: programmable waveform generator
